# Fritzing sketch Bubbler Electronics (saved by Fritzing 0.9.1b)
circuit board: 8.46667cm x 5.64444cm
breadboards: 1

parts:
  Part1 = Arduino Uno (Rev3)
  M1 = DC Motor
  Q1 = TRANSISTOR_NPN [package=to-92-ammo]
  R1 = Resistor [tolerance=±5% resistance=220 package=THT]
  D1 = Rectifier Diode [part_number=1N4001 package="300 mil [THT]"]
  PowerLED = LED - 5mm [color="Green (570nm)" package="5 mm [THT]"]
  Monitor_LED = LED - 5mm [color="Yellow (595nm)" package="5 mm [THT]"]
  Pressurising_LED = LED - 5mm [color="Orange (620nm)" package="5 mm [THT]"]
  R2 = Resistor [tolerance=±5% resistance=2.2k package=THT]
  R3 = Resistor [tolerance=±5% resistance=2.2k package=THT]
  R4 = Resistor [tolerance=±5% resistance=2.2k package=THT]
  R5 = Resistor [tolerance=±0.1% resistance=1k package=THT]
  R6 = Resistor [tolerance=±5% resistance=1M package=THT]
  HSC = IC, DIP package, 8 pins [chip_label=IC]

nets:
  N1: Part1.D12/MISO, HSC.pin7
  N2: Part1.D13/SCK, HSC.pin8
  N3: Part1.D3_PWM, R1.Pin_0
  N4: Part1.D4, Pressurising_LED.anode
  N5: Part1.D5_PWM, Monitor_LED.anode
  N6: Part1.D6_PWM, PowerLED.anode
  N7: Part1.D7, R5.Pin_1
  N8: Part1.5V, M1.pin_1, D1.cathode, R2.Pin_0, R3.Pin_0, R4.Pin_0, HSC.pin6
  N9: Part1.GND, Q1.E, R6.Pin_0, HSC.pin5
  N10: M1.pin_2, Q1.C, D1.anode
  N11: Q1.B, R1.Pin_1
  N12: PowerLED.cathode, R3.Pin_1
  N13: Monitor_LED.cathode, R4.Pin_1
  N14: Pressurising_LED.cathode, R2.Pin_1
  N15: R5.Pin_0, R6.Pin_1, HSC.pin1

// code stored in the sketch: Bubbler.ino
#include <SPI.h>
#include "pins.h"
#include "SSC.h"

SSC pressure_sensor(0x00, SELECT);

void printReading( float accumulator ) {
	Serial.print(pressure_sensor.pressure() * 70.3); // PSI to cm of water
	Serial.print(", ");
	Serial.print(pressure_sensor.temperature());
	Serial.print(", ");
	Serial.println(accumulator * 70.3);
	}

void chargePressureTube() {
	digitalWrite(MOTORLED, HIGH);
	float old_pressure = 0.0;
	float new_pressure = 0.0;
	float alpha = 0.3;
	float accumulator = 0.0;
	boolean charging = 1;
	boolean highpressure = 0;
	new_pressure = pressure_sensor.pressure();
	accumulator = new_pressure;

	while (charging) {
		accumulator = (alpha * new_pressure) + (1.0 - alpha) * accumulator;
		printReading(accumulator);
		highpressure = (new_pressure > (0.9 * pressure_sensor.maxPressure()));
		if (highpressure) {
			charging = 0;
			Serial.println("HIGH PRESSURE!");
			digitalWrite(WARNLED, HIGH);
			break;
			}
		else {
			digitalWrite(WARNLED, LOW);
			}
		if (charging) {
			digitalWrite(MOTOR, HIGH);
			int pump_duration = constrain(trunc(accumulator * 70.0), 25, 100);
			delay(pump_duration);
			digitalWrite(MOTOR, LOW);
			}
		delay(1000); // allow for pump motor inertia, and escape of some bubbles
		pressure_sensor.update();
		new_pressure = pressure_sensor.pressure();
		charging = (abs(new_pressure - accumulator) / accumulator > 0.01);
		}
	digitalWrite(MOTORLED, LOW);
	}

void readPressureGauge() {
	float old_pressure = pressure_sensor.pressure();
	float accumulator = old_pressure;
	float alpha = 0.3;
	boolean stable = 1;
	while (stable) {
		delay(10000);
		digitalWrite(READINGLED, HIGH);
		pressure_sensor.update();
		accumulator = (alpha * pressure_sensor.pressure()) + (1.0 - alpha) * accumulator;
		printReading(accumulator);
		digitalWrite(READINGLED, LOW);
		stable = (abs(old_pressure - accumulator) / old_pressure <= 0.01);
		}
	}

void setup() {
	// put your setup code here, to run once:
	setup_pins();
	Serial.begin(9600);
	pressure_sensor.setMinRaw(1638);
	pressure_sensor.setMaxRaw(14746);
	pressure_sensor.setMinPressure(0.0);
	pressure_sensor.setMaxPressure(5.0);
	pressure_sensor.setTemperatureCompensated(1);
	Serial.print("Initialising pressure sensor: ");
	Serial.println(pressure_sensor.start());
	Serial.print("Maximum pressure is ");
	Serial.println(pressure_sensor.maxPressure() * 70.3);
	pressure_sensor.update();
}

void loop() {
	// put your main code here, to run repeatedly:
	Serial.println(". o O ( Making Bubbles )");
	chargePressureTube();
	Serial.println(". o O ( Reading Pressure )");
	readPressureGauge();
}
